// Logisim project Glitch.circ as structural Verilog: 1 circuit, main circuit main
module main (
  input  X_0,
  input  X_1,
  input  X_2
);

  wire and_1_out, and_2_out, not_1_out, or_1_out;

  not not_1 (not_1_out, X_1);
  and and_1 (and_1_out, X_0, X_1);
  and and_2 (and_2_out, not_1_out, X_2);
  LED led_1 (.in(or_1_out));
  or or_1 (or_1_out, and_1_out, and_2_out);

  // Notes on the sheet:
  //   N
  //   AND_1
  //   AND_2
  //   y
endmodule
