// Logisim project CopyRegisters.circ as structural Verilog: 1 circuit, main circuit main
module main (
);

  wire and_1_out, and_2_out, and_3_out, and_4_out, and_5_out, and_6_out, and_7_out, and_8_out, button_1_out,
       s_r_ff_1_q, s_r_ff_1_qn, s_r_ff_3_q, s_r_ff_3_qn, s_r_ff_5_q, s_r_ff_5_qn, s_r_ff_7_q, s_r_ff_7_qn;

  Button button_1 (.out(button_1_out));
  S_R_Flip_Flop s_r_ff_1 (.Q(s_r_ff_1_q), .Qn(s_r_ff_1_qn));  // open: S, clk, R, preset, reset, en
  and and_1 (and_1_out, button_1_out, s_r_ff_1_q);
  and and_2 (and_2_out, button_1_out, s_r_ff_1_qn);
  S_R_Flip_Flop s_r_ff_2 (.S(and_1_out), .clk(and_1_out), .R(and_2_out));  // open: Q, Qn, preset, reset, en
  S_R_Flip_Flop s_r_ff_3 (.Q(s_r_ff_3_q), .Qn(s_r_ff_3_qn));  // open: S, clk, R, preset, reset, en
  and and_3 (and_3_out, button_1_out, s_r_ff_3_q);
  and and_4 (and_4_out, button_1_out, s_r_ff_3_qn);
  S_R_Flip_Flop s_r_ff_4 (.S(and_3_out), .clk(and_3_out), .R(and_4_out));  // open: Q, Qn, preset, reset, en
  S_R_Flip_Flop s_r_ff_5 (.Q(s_r_ff_5_q), .Qn(s_r_ff_5_qn));  // open: S, clk, R, preset, reset, en
  and and_5 (and_5_out, button_1_out, s_r_ff_5_q);
  and and_6 (and_6_out, button_1_out, s_r_ff_5_qn);
  S_R_Flip_Flop s_r_ff_6 (.S(and_5_out), .clk(and_5_out), .R(and_6_out));  // open: Q, Qn, preset, reset, en
  S_R_Flip_Flop s_r_ff_7 (.Q(s_r_ff_7_q), .Qn(s_r_ff_7_qn));  // open: S, clk, R, preset, reset, en
  and and_7 (and_7_out, button_1_out, s_r_ff_7_q);
  and and_8 (and_8_out, button_1_out, s_r_ff_7_qn);
  S_R_Flip_Flop s_r_ff_8 (.S(and_7_out), .clk(and_7_out), .R(and_8_out));  // open: Q, Qn, preset, reset, en

  // Notes on the sheet:
  //   Register A
  //   Register B
endmodule
