// Logisim project FlankenDetektor.circ as structural Verilog: 1 circuit, main circuit main
module main (
);

  wire and_1_out, not_1_out, not_2_out, not_3_out, undriven;

  not not_1 (not_1_out, undriven);
  not not_2 (not_2_out, not_1_out);
  not not_3 (not_3_out, not_2_out);
  and and_1 (and_1_out, undriven, not_3_out);

  // Notes on the sheet:
  //   E
  //   A
endmodule
