// Logisim project FlankengesteuertesShiftRegister.circ as structural Verilog: 1 circuit, main circuit main
module main (
  input  Clk,
  input  E_0,
  input  E_1
);

  wire and_1_out, and_2_out, and_3_out, and_4_out, and_5_out, and_6_out, and_7_out, and_8_out, s_r_ff_1_q,
       s_r_ff_1_qn, s_r_ff_2_q, s_r_ff_2_qn, s_r_ff_3_q, s_r_ff_3_qn;

  and and_1 (and_1_out, Clk, E_0);
  and and_2 (and_2_out, E_1, Clk);
  S_R_Flip_Flop s_r_ff_1 (
    .S(and_1_out), .R(and_2_out), .Q(s_r_ff_1_q), .Qn(s_r_ff_1_qn));  // open: clk, preset, reset, en
  and and_3 (and_3_out, Clk, s_r_ff_1_q);
  and and_4 (and_4_out, s_r_ff_1_qn, Clk);
  S_R_Flip_Flop s_r_ff_2 (
    .S(and_3_out), .R(and_4_out), .Q(s_r_ff_2_q), .Qn(s_r_ff_2_qn));  // open: clk, preset, reset, en
  and and_5 (and_5_out, Clk, s_r_ff_2_q);
  and and_6 (and_6_out, s_r_ff_2_qn, Clk);
  S_R_Flip_Flop s_r_ff_3 (
    .S(and_5_out), .R(and_6_out), .Q(s_r_ff_3_q), .Qn(s_r_ff_3_qn));  // open: clk, preset, reset, en
  and and_7 (and_7_out, Clk, s_r_ff_3_q);
  and and_8 (and_8_out, s_r_ff_3_qn, Clk);
  S_R_Flip_Flop s_r_ff_4 (.S(and_7_out), .R(and_8_out));  // open: clk, Q, Qn, preset, reset, en
endmodule
