// Logisim project JK_FlipFlop.circ as structural Verilog: 1 circuit, main circuit main
module main (
);

  wire nand_1_out, nand_2_out, nand_3_out, nand_4_out, not_1_out, not_2_out, not_3_out, undriven, undriven_2,
       undriven_3;

  not not_1 (not_1_out, undriven_2);
  not not_2 (not_2_out, not_1_out);
  not not_3 (not_3_out, not_2_out);
  nand nand_1 (nand_1_out, undriven, undriven_2, not_3_out, nand_4_out);
  nand nand_2 (nand_2_out, nand_3_out, not_3_out, undriven_2, undriven_3);
  nand nand_3 (nand_3_out, nand_1_out, nand_4_out);
  nand nand_4 (nand_4_out, nand_3_out, nand_2_out);

  // Notes on the sheet:
  //   J
  //   K
  //   S
  //   R
  //   Q
  //   Q
endmodule
