// Logisim project MasterSlave.circ as structural Verilog: 1 circuit, main circuit main
module main (
);

  wire not_1_out, s_r_ff_1_q, s_r_ff_1_qn, s_r_ff_2_q, s_r_ff_2_qn, undriven, undriven_2, undriven_3;

  not not_1 (not_1_out, undriven);
  S_R_Flip_Flop s_r_ff_1 (
    .S(undriven_2), .clk(undriven), .R(undriven_3), .Q(s_r_ff_1_q), .Qn(s_r_ff_1_qn));  // open: preset, reset, en
  S_R_Flip_Flop s_r_ff_2 (
    .S(s_r_ff_1_q), .clk(not_1_out), .R(s_r_ff_1_qn), .Q(s_r_ff_2_q), .Qn(s_r_ff_2_qn));  // open: preset, reset, en

  // Notes on the sheet:
  //   Clk
  //   S
  //   R
  //   Q
  //   Q
endmodule
