// Logisim project RS_with_NOR_and_NAND.circ as structural Verilog: 1 circuit, main circuit main
module main (
);

  wire nand_1_out, nand_2_out, nor_1_out, nor_2_out, undriven, undriven_2, undriven_3, undriven_4;

  nor nor_1 (nor_1_out, undriven, nor_2_out);
  nor nor_2 (nor_2_out, nor_1_out, undriven_2);
  nand nand_1 (nand_1_out, undriven_3, nand_2_out);
  nand nand_2 (nand_2_out, nand_1_out, undriven_4);

  // Notes on the sheet:
  //   S
  //   R
  //   _
  //   Q
  //   Q
  //   _
  //   S
  //   _
  //   R
  //   Q
  //   _
  //   Q
endmodule
