// Logisim project asynchronousLatch.circ as structural Verilog: 1 circuit, main circuit main
module main (
);

  wire nor_1_out, nor_2_out, nor_3_out, nor_4_out, undriven, undriven_2, undriven_3, undriven_4;

  nor nor_1 (nor_1_out, nor_2_out, undriven);
  nor nor_2 (nor_2_out, nor_1_out, undriven_2);
  nor nor_3 (nor_3_out, undriven_3, nor_4_out);
  nor nor_4 (nor_4_out, nor_3_out, undriven_4);

  // Notes on the sheet:
  //   S
  //   R
  //   Y
  //   S
  //   R
  //   Y
endmodule
