// Logisim project latch_temperature_monitoring.circ as structural Verilog: 1 circuit, main circuit main
module main (
  input  in_1
);

  wire button_1_out, s_r_ff_1_q;

  Button button_1 (.out(button_1_out));
  S_R_Flip_Flop s_r_ff_1 (.S(button_1_out), .R(in_1), .Q(s_r_ff_1_q));  // open: clk, Qn, preset, reset, en
  LED led_1 (.in(s_r_ff_1_q));

  // Notes on the sheet:
  //   Temperatursensor
  //   Reset
  //   Alarmleuchte
endmodule
