// Logisim project motivation_cycles.circ as structural Verilog: 1 circuit, main circuit main
module main (
  input  in_1,
  input  in_2,
  input  in_3
);

  wire nand_1_out, nor_1_out, not_1_out, not_2_out, not_3_out, or_1_out, s_r_ff_1_q, xnor_1_out;

  not not_1 (not_1_out, in_2);
  not not_2 (not_2_out, in_1);
  not not_3 (not_3_out, in_3);
  nand nand_1 (nand_1_out, s_r_ff_1_q, in_3, not_1_out);
  NotExactlyOne xnor_1 (.out(xnor_1_out), .in0(not_2_out), .in2(in_2), .in4(not_3_out));
  or or_1 (or_1_out, nand_1_out, xnor_1_out);
  nor nor_1 (nor_1_out, in_2, in_3);
  S_R_Flip_Flop s_r_ff_1 (.S(or_1_out), .R(nor_1_out), .Q(s_r_ff_1_q));  // open: clk, Qn, preset, reset, en

  // Notes on the sheet:
  //   Schaltnetz I
  //   Kombinatorisches
  //   Kombinatorisches
  //   Schaltnetz II
endmodule
