// Logisim project rs_latch.circ as structural Verilog: 1 circuit, main circuit main
module main (
);

  wire and_1_out, not_1_out, or_1_out, undriven, undriven_2;

  or or_1 (or_1_out, and_1_out, undriven);
  not not_1 (not_1_out, undriven_2);
  and and_1 (and_1_out, or_1_out, not_1_out);

  // Notes on the sheet:
  //   S
  //   R
  //   Y
endmodule
