// Logisim project Schaltwerk_Detektor.circ as structural Verilog: 2 circuits, main circuit main
module main (
  input  E
);

  wire clock_1_out, F_q, F_qn, G_q, G_qn, Gatter_out_6, Gatter_out_7, Gatter_out_8;

  Clock clock_1 (.out(clock_1_out));
  Gatter Gatter (
    .in_1(E), .in_2(F_q), .in_3(F_qn), .in_4(G_q), .in_5(G_qn), .out_6(Gatter_out_6), .out_7(Gatter_out_7),
    .out_8(Gatter_out_8));
  D_Flip_Flop F (.clk(clock_1_out), .D(Gatter_out_6), .Q(F_q), .Qn(F_qn));  // open: preset, en, reset
  D_Flip_Flop G (.clk(clock_1_out), .D(Gatter_out_7), .Q(G_q), .Qn(G_qn));  // open: preset, en, reset
  LED led_1 (.in(Gatter_out_8));

  // Notes on the sheet:
  //   Clock
  //   A
endmodule

module Gatter (
  input  in_1,
  input  in_2,
  input  in_3,
  input  in_4,
  input  in_5,
  output out_6,
  output out_7,
  output out_8
);
endmodule
